# Fritzing sketch solarem1 (saved by Fritzing 0.9.3b)
breadboards: 1

parts:
  Raspberry_Pi_1 = Raspberry Pi 3 [part_number=RPI-3-V1.2]
  IC1 = Voltage Regulator [package=to-220-alt]
  C1 = Electrolytic Capacitor [capacitance=10µF package="100 mil [THT, electrolytic]"]
  C2 = Electrolytic Capacitor [capacitance=22µF package="100 mil [THT, electrolytic]"]
  JP1 = Header 2 [package=jst-2-smd-vert]
  JP1_2 = Header 2 [package=screwterminal-3.5mm-2_lock]
  JP2 = Header 2 [package=screwterminal-3.5mm-2_lock]
  J1 = Camdenboss CTB0158-10 [part_number=8-Relettä package=THT]
  J2 = Camdenboss CTB0158-3 [part_number=8-relettä package=THT]

nets:
  GND: Raspberry_Pi_1.GND, C1.-, C2.-, JP1.2, JP1_2.2, JP2.2, J1.GND, J2.GND
  N1: Raspberry_Pi_1.GPIO17, J1.IN8
  N2: Raspberry_Pi_1.GPIO10, J1.IN1
  N3: Raspberry_Pi_1.GPIO11, J1.IN2
  N4: Raspberry_Pi_1.GPIO13, J1.IN4
  N5: Raspberry_Pi_1.GPIO16, J1.IN7
  N6: Raspberry_Pi_1.GPIO12, J1.IN3
  N7: Raspberry_Pi_1.GPIO15, J1.IN6
  N8: Raspberry_Pi_1.GPIO14, J1.IN5
  N9: IC1.IN, C1.+, JP1.1, JP1_2.1
  N10: IC1.OUT, C2.+, JP2.1, J2.VCC

custom parts:
  Camdenboss CTB0158-10: Camdenboss CTB0158-10 5.08mm (0.2") Pitch Standard Profile 90 ̊ Rising Clamp Terminal, 10 pole The real-life connectors are modular, made up of two or three connector blocks slotted together. These can be further slotted together to make larger connectors. Fritzing part is derived from Screw terminals by Lionel Michel. Because of the offset between connection pins and screw terminals, these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
  Camdenboss CTB0158-3: Camdenboss CTB0158-3 5.08mm (0.2") Pitch Standard Profile 90 ̊ Rising Clamp Terminal, 3 pole The real-life connectors are modular, made up of two or three connector blocks slotted together. These can be further slotted together to make larger connectors. Fritzing part is derived from Screw terminals by Lionel Michel. Because of the offset between connection pins and screw terminals, these are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
